// Logisim project ULA.circ as structural Verilog: 10 circuits, main circuit main
module main (
  input  [31:0] Entrada_A,
  input  [31:0] Entrada_B,
  input  [4:0] Seletor,
  output out_4,
  output [31:0] \Saída_S 
);

  wire and_1_out, and_2_out, and_3_out, celula_1_cout, celula_2_cout, celula_3_cout, celula_4_cout,
       celula_5_cout, celula_6_cout, celula_7_cout, celula_8_cout, celula_9_cout, celula_10_cout,
       celula_11_cout, celula_12_cout, celula_13_cout, celula_14_cout, celula_15_cout, celula_16_cout,
       celula_17_cout, celula_18_cout, celula_19_cout, celula_20_cout, celula_21_cout, celula_22_cout,
       celula_23_cout, celula_24_cout, celula_25_cout, celula_26_cout, celula_27_cout, celula_28_cout,
       celula_29_cout, celula_30_cout, celula_31_cout, celula_32_cout, overflowcontroler_1_overflow;
  wire [31:0] celula_31_s, \SLL_saída_a , \SRA_saída_a , \SRL_saída_a ;

  SLL SLL (.Entrada_A(Entrada_A), .Seletor(and_1_out), .\Saída_A (\SLL_saída_a ));
  SRL SRL (.Entrada_A(Entrada_A), .in_2(and_2_out), .\Saída_A (\SRL_saída_a ));
  SRA SRA (.Entrada_A(Entrada_A), .in_2(and_3_out), .\Saída_A (\SRA_saída_a ));
  Multiplexer #(.select(5), .width(32), .enable("false")) multiplexer_1 (
    .in0(celula_31_s), .in1(celula_31_s), .in2(celula_31_s), .in3(celula_31_s), .in4(celula_31_s),
    .in5(celula_31_s), .in6(celula_31_s), .in7(\SLL_saída_a ), .in8(\SRL_saída_a ), .in9(\SRA_saída_a ),
    .out(\Saída_S ), .sel(Seletor));  // open: in10, in11, in12, in13, in14, in15, in16, in17, in18, in19, in20, in21, in22, in23, in24, in25, in26, in27, in28, in29, in30, in31
  and and_1 (and_1_out, Seletor[0], Seletor[1], Seletor[2], ~Seletor[3], ~Seletor[4]);  // AND_Gate
  and and_2 (and_2_out, ~Seletor[0], ~Seletor[1], ~Seletor[2], Seletor[3], ~Seletor[4]);  // AND_Gate
  and and_3 (and_3_out, Seletor[0], ~Seletor[1], ~Seletor[2], Seletor[3], ~Seletor[4]);  // AND_Gate
  Celula celula_1 (
    .Cin(celula_2_cout), .Cout(celula_1_cout), .b(Entrada_B[30]), .a(Entrada_A[30]), .Seletor(Seletor),
    .S(celula_31_s[30]));
  Celula celula_2 (
    .Cin(celula_4_cout), .Cout(celula_2_cout), .b(Entrada_B[31]), .a(Entrada_A[31]), .Seletor(Seletor),
    .S(celula_31_s[31]));
  Celula celula_3 (
    .Cin(celula_1_cout), .Cout(celula_3_cout), .b(Entrada_B[28]), .a(Entrada_A[28]), .Seletor(Seletor),
    .S(celula_31_s[28]));
  Celula celula_4 (
    .Cin(celula_6_cout), .Cout(celula_4_cout), .b(Entrada_B[29]), .a(Entrada_A[29]), .Seletor(Seletor),
    .S(celula_31_s[29]));
  Celula celula_5 (
    .Cin(celula_3_cout), .Cout(celula_5_cout), .b(Entrada_B[26]), .a(Entrada_A[26]), .Seletor(Seletor),
    .S(celula_31_s[26]));
  Celula celula_6 (
    .Cin(celula_8_cout), .Cout(celula_6_cout), .b(Entrada_B[27]), .a(Entrada_A[27]), .Seletor(Seletor),
    .S(celula_31_s[27]));
  Celula celula_7 (
    .Cin(celula_5_cout), .Cout(celula_7_cout), .b(Entrada_B[24]), .a(Entrada_A[24]), .Seletor(Seletor),
    .S(celula_31_s[24]));
  Celula celula_8 (
    .Cin(celula_10_cout), .Cout(celula_8_cout), .b(Entrada_B[25]), .a(Entrada_A[25]), .Seletor(Seletor),
    .S(celula_31_s[25]));
  Celula celula_9 (
    .Cin(celula_7_cout), .Cout(celula_9_cout), .b(Entrada_B[23]), .a(Entrada_A[22]), .Seletor(Seletor),
    .S(celula_31_s[22]));
  Celula celula_10 (
    .Cin(celula_12_cout), .Cout(celula_10_cout), .b(Entrada_B[22]), .a(Entrada_A[23]), .Seletor(Seletor),
    .S(celula_31_s[23]));
  Celula celula_11 (
    .Cin(celula_9_cout), .Cout(celula_11_cout), .b(Entrada_B[21]), .a(Entrada_A[20]), .Seletor(Seletor),
    .S(celula_31_s[20]));
  Celula celula_12 (
    .Cin(celula_14_cout), .Cout(celula_12_cout), .b(Entrada_B[20]), .a(Entrada_A[21]), .Seletor(Seletor),
    .S(celula_31_s[21]));
  Celula celula_13 (
    .Cin(celula_11_cout), .Cout(celula_13_cout), .b(Entrada_B[19]), .a(Entrada_A[18]), .Seletor(Seletor),
    .S(celula_31_s[18]));
  Celula celula_14 (
    .Cin(celula_16_cout), .Cout(celula_14_cout), .b(Entrada_B[18]), .a(Entrada_A[19]), .Seletor(Seletor),
    .S(celula_31_s[19]));
  Celula celula_15 (
    .Cin(celula_13_cout), .Cout(celula_15_cout), .b(Entrada_B[17]), .a(Entrada_A[16]), .Seletor(Seletor),
    .S(celula_31_s[16]));
  Celula celula_16 (
    .Cin(celula_18_cout), .Cout(celula_16_cout), .b(Entrada_B[16]), .a(Entrada_A[17]), .Seletor(Seletor),
    .S(celula_31_s[17]));
  Celula celula_17 (
    .Cin(celula_15_cout), .Cout(celula_17_cout), .b(Entrada_B[15]), .a(Entrada_A[14]), .Seletor(Seletor),
    .S(celula_31_s[14]));
  Celula celula_18 (
    .Cin(celula_20_cout), .Cout(celula_18_cout), .b(Entrada_B[14]), .a(Entrada_A[15]), .Seletor(Seletor),
    .S(celula_31_s[15]));
  Celula celula_19 (
    .Cin(celula_17_cout), .Cout(celula_19_cout), .b(Entrada_B[13]), .a(Entrada_A[12]), .Seletor(Seletor),
    .S(celula_31_s[12]));
  Celula celula_20 (
    .Cin(celula_22_cout), .Cout(celula_20_cout), .b(Entrada_B[12]), .a(Entrada_A[13]), .Seletor(Seletor),
    .S(celula_31_s[13]));
  Celula celula_21 (
    .Cin(celula_19_cout), .Cout(celula_21_cout), .b(Entrada_B[11]), .a(Entrada_A[10]), .Seletor(Seletor),
    .S(celula_31_s[10]));
  Celula celula_22 (
    .Cin(celula_24_cout), .Cout(celula_22_cout), .b(Entrada_B[10]), .a(Entrada_A[11]), .Seletor(Seletor),
    .S(celula_31_s[11]));
  Celula celula_23 (
    .Cin(celula_21_cout), .Cout(celula_23_cout), .b(Entrada_B[9]), .a(Entrada_A[8]), .Seletor(Seletor),
    .S(celula_31_s[8]));
  Celula celula_24 (
    .Cin(celula_26_cout), .Cout(celula_24_cout), .b(Entrada_B[8]), .a(Entrada_A[9]), .Seletor(Seletor),
    .S(celula_31_s[9]));
  Celula celula_25 (
    .Cin(celula_23_cout), .Cout(celula_25_cout), .b(Entrada_B[7]), .a(Entrada_A[6]), .Seletor(Seletor),
    .S(celula_31_s[6]));
  Celula celula_26 (
    .Cin(celula_28_cout), .Cout(celula_26_cout), .b(Entrada_B[6]), .a(Entrada_A[7]), .Seletor(Seletor),
    .S(celula_31_s[7]));
  Celula celula_27 (
    .Cin(celula_25_cout), .Cout(celula_27_cout), .b(Entrada_B[5]), .a(Entrada_A[4]), .Seletor(Seletor),
    .S(celula_31_s[4]));
  Celula celula_28 (
    .Cin(celula_30_cout), .Cout(celula_28_cout), .b(Entrada_B[4]), .a(Entrada_A[5]), .Seletor(Seletor),
    .S(celula_31_s[5]));
  Celula celula_29 (
    .Cin(celula_27_cout), .Cout(celula_29_cout), .b(Entrada_B[3]), .a(Entrada_A[2]), .Seletor(Seletor),
    .S(celula_31_s[2]));
  Celula celula_30 (
    .Cin(celula_32_cout), .Cout(celula_30_cout), .b(Entrada_B[2]), .a(Entrada_A[3]), .Seletor(Seletor),
    .S(celula_31_s[3]));
  Celula celula_31 (
    .Cin(celula_29_cout), .Cout(celula_31_cout), .b(Entrada_B[1]), .a(Entrada_A[0]), .Seletor(Seletor),
    .S(celula_31_s[0]));
  Celula celula_32 (
    .Cin(1'b0), .Cout(celula_32_cout), .b(Entrada_B[0]), .a(Entrada_A[1]), .Seletor(Seletor),
    .S(celula_31_s[1]));
  OverFlowControler overflowcontroler_1 (
    .Overflow(overflowcontroler_1_overflow), .Cin(celula_31_cout), .Seletor(Seletor), .a(Entrada_A[0]),
    .b(Entrada_B[1]), .s(celula_31_s[0]));

  // Notes on the sheet:
  //   00000=AND
  //   00001=OR
  //   00010=XOR
  //   00011=NAND
  //   00100=SOMA INT
  //   00101=SOMA NAT
  //   00110=SUBTRAIR
  //   00111=DESLOCAMENTO ESQUERDA
  //   01000=DESLOCAMENTO DIREITA
  //   01001=DESLOCAMENTO DIREITA ARIT
  //   Overflow
endmodule

module Celula (
  input  Cin,
  input  b,
  input  a,
  input  [4:0] Seletor,
  output S,
  output Cout
);

  wire and_1_out, and_2_out, nand_1_out, or_1_out, Somador_s, Somador_vai1, Subtrator_s, Subtrator_vai1,
       xor_1_out;

  and and_1 (and_1_out, a, b);
  or or_1 (or_1_out, a, b);
  xor xor_1 (xor_1_out, a, b);
  nand nand_1 (nand_1_out, a, b);
  Somador Somador (.a(a), .b(b), .Vem1(Cin), .Vai1(Somador_vai1), .S(Somador_s));
  Subtrator Subtrator (.a(a), .b(b), .Vem1(Cin), .Vai1(Subtrator_vai1), .S(Subtrator_s));
  Multiplexer #(.enable("false")) multiplexer_1 (.in0(Somador_vai1), .in1(Subtrator_vai1), .out(Cout), .sel(and_2_out));
  and and_2 (and_2_out, ~Seletor[0], Seletor[1], Seletor[2], ~Seletor[3], ~Seletor[4]);  // AND_Gate
  Multiplexer #(.select(5), .enable("false")) multiplexer_2 (
    .in0(and_1_out), .in1(or_1_out), .in2(xor_1_out), .in3(nand_1_out), .in4(Somador_s), .in5(Somador_s),
    .in6(Subtrator_s), .in7(a), .in8(a), .in9(a), .out(S), .sel(Seletor));  // open: in10, in11, in12, in13, in14, in15, in16, in17, in18, in19, in20, in21, in22, in23, in24, in25, in26, in27, in28, in29, in30, in31

  // Notes on the sheet:
  //   00000=AND
  //   00001=OR
  //   00010=XOR
  //   00011=NAND
  //   00100=SOMA INT
  //   00101=SOMA NAT
  //   00110=SUBTRATOR
  //   00111=DESLOCAMENTO ESQUERDA
  //   01000=DESLOCAMENTO DIREITA
endmodule

module OverFlowControler (
  input  Cin,
  input  a,
  input  b,
  input  s,
  input  [4:0] Seletor,
  output Overflow
);

  wire and_1_out, and_2_out, and_3_out, or_1_out;

  Multiplexer #(.enable("false")) multiplexer_1 (.in0(Cin), .in1(or_1_out), .out(Overflow), .sel(and_1_out));
  and and_1 (and_1_out, Seletor[0], ~Seletor[1], Seletor[2], ~Seletor[3], ~Seletor[4]);  // AND_Gate
  or or_1 (or_1_out, and_2_out, and_3_out);
  and and_2 (and_2_out, a, b, ~s);  // AND_Gate
  and and_3 (and_3_out, ~a, ~b, s);  // AND_Gate

  // Notes on the sheet:
  //   00100 - Soma de Naturais
  //   00101 - Soma de Inteiros
endmodule

module Somador (
  input  Vem1,
  input  a,
  input  b,
  output S,
  output Vai1
);

  wire and_1_out, and_2_out, and_3_out, xor_1_out;

  and and_1 (and_1_out, b, a);
  and and_2 (and_2_out, b, Vem1);
  or or_1 (Vai1, and_1_out, and_2_out, and_3_out);
  and and_3 (and_3_out, a, Vem1);
  xor xor_1 (xor_1_out, a, b);
  xor xor_2 (S, Vem1, xor_1_out);
endmodule

module Subtrator (
  input  Vem1,
  input  a,
  input  b,
  output S,
  output Vai1
);

  wire and_1_out, and_2_out, and_3_out, xor_1_out;

  and and_1 (and_1_out, b, ~a);  // AND_Gate
  and and_2 (and_2_out, b, Vem1);
  or or_1 (Vai1, and_1_out, and_2_out, and_3_out);
  and and_3 (and_3_out, ~a, Vem1);  // AND_Gate
  xor xor_1 (xor_1_out, a, b);
  xor xor_2 (S, Vem1, xor_1_out);
endmodule

module SRL (
  input  [31:0] Entrada_A,
  input  in_2,
  output [31:0] \Saída_A 
);

  Multiplexer #(.enable("false")) multiplexer_1 (.in0(Entrada_A[31]), .in1(1'b0), .out(\Saída_A [31]), .sel(in_2));
  Multiplexer #(.enable("false")) multiplexer_2 (
    .in0(Entrada_A[30]), .in1(Entrada_A[31]), .out(\Saída_A [30]), .sel(in_2));
  Multiplexer #(.enable("false")) multiplexer_3 (
    .in0(Entrada_A[29]), .in1(Entrada_A[30]), .out(\Saída_A [29]), .sel(in_2));
  Multiplexer #(.enable("false")) multiplexer_4 (
    .in0(Entrada_A[28]), .in1(Entrada_A[29]), .out(\Saída_A [28]), .sel(in_2));
  Multiplexer #(.enable("false")) multiplexer_5 (
    .in0(Entrada_A[27]), .in1(Entrada_A[28]), .out(\Saída_A [27]), .sel(in_2));
  Multiplexer #(.enable("false")) multiplexer_6 (
    .in0(Entrada_A[26]), .in1(Entrada_A[27]), .out(\Saída_A [26]), .sel(in_2));
  Multiplexer #(.enable("false")) multiplexer_7 (
    .in0(Entrada_A[25]), .in1(Entrada_A[26]), .out(\Saída_A [25]), .sel(in_2));
  Multiplexer #(.enable("false")) multiplexer_8 (
    .in0(Entrada_A[24]), .in1(Entrada_A[25]), .out(\Saída_A [24]), .sel(in_2));
  Multiplexer #(.enable("false")) multiplexer_9 (
    .in0(Entrada_A[23]), .in1(Entrada_A[24]), .out(\Saída_A [23]), .sel(in_2));
  Multiplexer #(.enable("false")) multiplexer_10 (
    .in0(Entrada_A[22]), .in1(Entrada_A[23]), .out(\Saída_A [22]), .sel(in_2));
  Multiplexer #(.enable("false")) multiplexer_11 (
    .in0(Entrada_A[21]), .in1(Entrada_A[22]), .out(\Saída_A [21]), .sel(in_2));
  Multiplexer #(.enable("false")) multiplexer_12 (
    .in0(Entrada_A[20]), .in1(Entrada_A[21]), .out(\Saída_A [20]), .sel(in_2));
  Multiplexer #(.enable("false")) multiplexer_13 (
    .in0(Entrada_A[19]), .in1(Entrada_A[20]), .out(\Saída_A [19]), .sel(in_2));
  Multiplexer #(.enable("false")) multiplexer_14 (
    .in0(Entrada_A[18]), .in1(Entrada_A[19]), .out(\Saída_A [18]), .sel(in_2));
  Multiplexer #(.enable("false")) multiplexer_15 (
    .in0(Entrada_A[17]), .in1(Entrada_A[18]), .out(\Saída_A [17]), .sel(in_2));
  Multiplexer #(.enable("false")) multiplexer_16 (
    .in0(Entrada_A[16]), .in1(Entrada_A[17]), .out(\Saída_A [16]), .sel(in_2));
  Multiplexer #(.enable("false")) multiplexer_17 (
    .in0(Entrada_A[15]), .in1(Entrada_A[16]), .out(\Saída_A [15]), .sel(in_2));
  Multiplexer #(.enable("false")) multiplexer_18 (
    .in0(Entrada_A[14]), .in1(Entrada_A[15]), .out(\Saída_A [14]), .sel(in_2));
  Multiplexer #(.enable("false")) multiplexer_19 (
    .in0(Entrada_A[13]), .in1(Entrada_A[14]), .out(\Saída_A [13]), .sel(in_2));
  Multiplexer #(.enable("false")) multiplexer_20 (
    .in0(Entrada_A[12]), .in1(Entrada_A[13]), .out(\Saída_A [12]), .sel(in_2));
  Multiplexer #(.enable("false")) multiplexer_21 (
    .in0(Entrada_A[11]), .in1(Entrada_A[12]), .out(\Saída_A [11]), .sel(in_2));
  Multiplexer #(.enable("false")) multiplexer_22 (
    .in0(Entrada_A[10]), .in1(Entrada_A[11]), .out(\Saída_A [10]), .sel(in_2));
  Multiplexer #(.enable("false")) multiplexer_23 (
    .in0(Entrada_A[9]), .in1(Entrada_A[10]), .out(\Saída_A [9]), .sel(in_2));
  Multiplexer #(.enable("false")) multiplexer_24 (
    .in0(Entrada_A[8]), .in1(Entrada_A[9]), .out(\Saída_A [8]), .sel(in_2));
  Multiplexer #(.enable("false")) multiplexer_25 (
    .in0(Entrada_A[7]), .in1(Entrada_A[8]), .out(\Saída_A [7]), .sel(in_2));
  Multiplexer #(.enable("false")) multiplexer_26 (
    .in0(Entrada_A[6]), .in1(Entrada_A[7]), .out(\Saída_A [6]), .sel(in_2));
  Multiplexer #(.enable("false")) multiplexer_27 (
    .in0(Entrada_A[5]), .in1(Entrada_A[6]), .out(\Saída_A [5]), .sel(in_2));
  Multiplexer #(.enable("false")) multiplexer_28 (
    .in0(Entrada_A[4]), .in1(Entrada_A[5]), .out(\Saída_A [4]), .sel(in_2));
  Multiplexer #(.enable("false")) multiplexer_29 (
    .in0(Entrada_A[3]), .in1(Entrada_A[4]), .out(\Saída_A [3]), .sel(in_2));
  Multiplexer #(.enable("false")) multiplexer_30 (
    .in0(Entrada_A[2]), .in1(Entrada_A[3]), .out(\Saída_A [2]), .sel(in_2));
  Multiplexer #(.enable("false")) multiplexer_31 (
    .in0(Entrada_A[1]), .in1(Entrada_A[2]), .out(\Saída_A [1]), .sel(in_2));
  Multiplexer #(.enable("false")) multiplexer_32 (
    .in0(Entrada_A[0]), .in1(Entrada_A[1]), .out(\Saída_A [0]), .sel(in_2));
endmodule

module DeslocadorCompleto4 (
  input  in_1,
  input  in_2,
  input  in_3,
  input  in_4,
  input  [1:0] in_5,
  output out_6,
  output out_7,
  output out_8,
  output out_9
);

  wire multiplexer_1_out, multiplexer_2_out, multiplexer_3_out, multiplexer_5_out, multiplexer_6_out,
       multiplexer_7_out, multiplexer_9_out, multiplexer_10_out, multiplexer_11_out, multiplexer_13_out,
       multiplexer_14_out, multiplexer_15_out, seldeslocadorc4_1_s0, seldeslocadorc4_1_s1,
       seldeslocadorc4_1_s2, undriven;

  Multiplexer #(.enable("false")) multiplexer_1 (
    .in0(in_1), .in1(1'b0), .out(multiplexer_1_out), .sel(seldeslocadorc4_1_s0));
  Multiplexer #(.enable("false")) multiplexer_2 (
    .in0(multiplexer_1_out), .in1(1'b0), .out(multiplexer_2_out), .sel(seldeslocadorc4_1_s1));
  Multiplexer #(.enable("false")) multiplexer_3 (
    .in0(multiplexer_2_out), .in1(1'b0), .out(multiplexer_3_out), .sel(seldeslocadorc4_1_s2));
  Multiplexer #(.enable("false")) multiplexer_4 (.in0(multiplexer_3_out), .in1(1'b0), .out(out_6), .sel(undriven));
  Multiplexer #(.enable("false")) multiplexer_5 (
    .in0(in_2), .in1(in_1), .out(multiplexer_5_out), .sel(seldeslocadorc4_1_s0));
  Multiplexer #(.enable("false")) multiplexer_6 (
    .in0(multiplexer_5_out), .in1(multiplexer_1_out), .out(multiplexer_6_out), .sel(seldeslocadorc4_1_s1));
  Multiplexer #(.enable("false")) multiplexer_7 (
    .in0(multiplexer_6_out), .in1(multiplexer_2_out), .out(multiplexer_7_out), .sel(seldeslocadorc4_1_s2));
  Multiplexer #(.enable("false")) multiplexer_8 (
    .in0(multiplexer_7_out), .in1(multiplexer_3_out), .out(out_7), .sel(undriven));
  Multiplexer #(.enable("false")) multiplexer_9 (
    .in0(in_3), .in1(in_2), .out(multiplexer_9_out), .sel(seldeslocadorc4_1_s0));
  Multiplexer #(.enable("false")) multiplexer_10 (
    .in0(multiplexer_9_out), .in1(multiplexer_5_out), .out(multiplexer_10_out), .sel(seldeslocadorc4_1_s1));
  Multiplexer #(.enable("false")) multiplexer_11 (
    .in0(multiplexer_10_out), .in1(multiplexer_6_out), .out(multiplexer_11_out), .sel(seldeslocadorc4_1_s2));
  Multiplexer #(.enable("false")) multiplexer_12 (
    .in0(multiplexer_11_out), .in1(multiplexer_7_out), .out(out_8), .sel(undriven));
  Multiplexer #(.enable("false")) multiplexer_13 (
    .in0(in_4), .in1(in_3), .out(multiplexer_13_out), .sel(seldeslocadorc4_1_s0));
  Multiplexer #(.enable("false")) multiplexer_14 (
    .in0(multiplexer_13_out), .in1(multiplexer_9_out), .out(multiplexer_14_out), .sel(seldeslocadorc4_1_s1));
  Multiplexer #(.enable("false")) multiplexer_15 (
    .in0(multiplexer_14_out), .in1(multiplexer_10_out), .out(multiplexer_15_out), .sel(seldeslocadorc4_1_s2));
  Multiplexer #(.enable("false")) multiplexer_16 (
    .in0(multiplexer_15_out), .in1(multiplexer_11_out), .out(out_9), .sel(undriven));
  SelDeslocadorC4 seldeslocadorc4_1 (
    .A(in_5[1]), .B(in_5[0]), .S0(seldeslocadorc4_1_s0), .S1(seldeslocadorc4_1_s1), .S2(seldeslocadorc4_1_s2));
endmodule

module SelDeslocadorC4 (
  input  A,
  input  B,
  output S0,
  output S1,
  output S2
);

  or or_1 (S0, B, A);
  and and_1 (S2, B, A);

  assign S1 = A;
endmodule

module SLL (
  input  [31:0] Entrada_A,
  input  Seletor,
  output [31:0] \Saída_A 
);

  Multiplexer #(.enable("false")) multiplexer_1 (
    .in0(Entrada_A[31]), .in1(Entrada_A[30]), .out(\Saída_A [31]), .sel(Seletor));
  Multiplexer #(.enable("false")) multiplexer_2 (
    .in0(Entrada_A[30]), .in1(Entrada_A[29]), .out(\Saída_A [30]), .sel(Seletor));
  Multiplexer #(.enable("false")) multiplexer_3 (
    .in0(Entrada_A[29]), .in1(Entrada_A[28]), .out(\Saída_A [29]), .sel(Seletor));
  Multiplexer #(.enable("false")) multiplexer_4 (
    .in0(Entrada_A[28]), .in1(Entrada_A[27]), .out(\Saída_A [28]), .sel(Seletor));
  Multiplexer #(.enable("false")) multiplexer_5 (
    .in0(Entrada_A[27]), .in1(Entrada_A[26]), .out(\Saída_A [27]), .sel(Seletor));
  Multiplexer #(.enable("false")) multiplexer_6 (
    .in0(Entrada_A[26]), .in1(Entrada_A[25]), .out(\Saída_A [26]), .sel(Seletor));
  Multiplexer #(.enable("false")) multiplexer_7 (
    .in0(Entrada_A[25]), .in1(Entrada_A[24]), .out(\Saída_A [25]), .sel(Seletor));
  Multiplexer #(.enable("false")) multiplexer_8 (
    .in0(Entrada_A[24]), .in1(Entrada_A[23]), .out(\Saída_A [24]), .sel(Seletor));
  Multiplexer #(.enable("false")) multiplexer_9 (
    .in0(Entrada_A[23]), .in1(Entrada_A[22]), .out(\Saída_A [23]), .sel(Seletor));
  Multiplexer #(.enable("false")) multiplexer_10 (
    .in0(Entrada_A[22]), .in1(Entrada_A[21]), .out(\Saída_A [22]), .sel(Seletor));
  Multiplexer #(.enable("false")) multiplexer_11 (
    .in0(Entrada_A[21]), .in1(Entrada_A[20]), .out(\Saída_A [21]), .sel(Seletor));
  Multiplexer #(.enable("false")) multiplexer_12 (
    .in0(Entrada_A[20]), .in1(Entrada_A[19]), .out(\Saída_A [20]), .sel(Seletor));
  Multiplexer #(.enable("false")) multiplexer_13 (
    .in0(Entrada_A[19]), .in1(Entrada_A[18]), .out(\Saída_A [19]), .sel(Seletor));
  Multiplexer #(.enable("false")) multiplexer_14 (
    .in0(Entrada_A[18]), .in1(Entrada_A[17]), .out(\Saída_A [18]), .sel(Seletor));
  Multiplexer #(.enable("false")) multiplexer_15 (
    .in0(Entrada_A[17]), .in1(Entrada_A[16]), .out(\Saída_A [17]), .sel(Seletor));
  Multiplexer #(.enable("false")) multiplexer_16 (
    .in0(Entrada_A[16]), .in1(Entrada_A[15]), .out(\Saída_A [16]), .sel(Seletor));
  Multiplexer #(.enable("false")) multiplexer_17 (
    .in0(Entrada_A[15]), .in1(Entrada_A[14]), .out(\Saída_A [15]), .sel(Seletor));
  Multiplexer #(.enable("false")) multiplexer_18 (
    .in0(Entrada_A[14]), .in1(Entrada_A[13]), .out(\Saída_A [14]), .sel(Seletor));
  Multiplexer #(.enable("false")) multiplexer_19 (
    .in0(Entrada_A[13]), .in1(Entrada_A[12]), .out(\Saída_A [13]), .sel(Seletor));
  Multiplexer #(.enable("false")) multiplexer_20 (
    .in0(Entrada_A[12]), .in1(Entrada_A[11]), .out(\Saída_A [12]), .sel(Seletor));
  Multiplexer #(.enable("false")) multiplexer_21 (
    .in0(Entrada_A[11]), .in1(Entrada_A[10]), .out(\Saída_A [11]), .sel(Seletor));
  Multiplexer #(.enable("false")) multiplexer_22 (
    .in0(Entrada_A[10]), .in1(Entrada_A[9]), .out(\Saída_A [10]), .sel(Seletor));
  Multiplexer #(.enable("false")) multiplexer_23 (
    .in0(Entrada_A[9]), .in1(Entrada_A[8]), .out(\Saída_A [9]), .sel(Seletor));
  Multiplexer #(.enable("false")) multiplexer_24 (
    .in0(Entrada_A[8]), .in1(Entrada_A[7]), .out(\Saída_A [8]), .sel(Seletor));
  Multiplexer #(.enable("false")) multiplexer_25 (
    .in0(Entrada_A[7]), .in1(Entrada_A[6]), .out(\Saída_A [7]), .sel(Seletor));
  Multiplexer #(.enable("false")) multiplexer_26 (
    .in0(Entrada_A[6]), .in1(Entrada_A[5]), .out(\Saída_A [6]), .sel(Seletor));
  Multiplexer #(.enable("false")) multiplexer_27 (
    .in0(Entrada_A[5]), .in1(Entrada_A[4]), .out(\Saída_A [5]), .sel(Seletor));
  Multiplexer #(.enable("false")) multiplexer_28 (
    .in0(Entrada_A[4]), .in1(Entrada_A[3]), .out(\Saída_A [4]), .sel(Seletor));
  Multiplexer #(.enable("false")) multiplexer_29 (
    .in0(Entrada_A[3]), .in1(Entrada_A[2]), .out(\Saída_A [3]), .sel(Seletor));
  Multiplexer #(.enable("false")) multiplexer_30 (
    .in0(Entrada_A[2]), .in1(Entrada_A[1]), .out(\Saída_A [2]), .sel(Seletor));
  Multiplexer #(.enable("false")) multiplexer_31 (
    .in0(Entrada_A[1]), .in1(Entrada_A[0]), .out(\Saída_A [1]), .sel(Seletor));
  Multiplexer #(.enable("false")) multiplexer_32 (.in0(Entrada_A[0]), .in1(1'b0), .out(\Saída_A [0]), .sel(Seletor));
endmodule

module SRA (
  input  [31:0] Entrada_A,
  input  in_2,
  output [31:0] \Saída_A 
);

  Multiplexer #(.enable("false")) multiplexer_1 (
    .in0(Entrada_A[31]), .in1(Entrada_A[31]), .out(\Saída_A [31]), .sel(in_2));
  Multiplexer #(.enable("false")) multiplexer_2 (
    .in0(Entrada_A[30]), .in1(Entrada_A[31]), .out(\Saída_A [30]), .sel(in_2));
  Multiplexer #(.enable("false")) multiplexer_3 (
    .in0(Entrada_A[29]), .in1(Entrada_A[30]), .out(\Saída_A [29]), .sel(in_2));
  Multiplexer #(.enable("false")) multiplexer_4 (
    .in0(Entrada_A[28]), .in1(Entrada_A[29]), .out(\Saída_A [28]), .sel(in_2));
  Multiplexer #(.enable("false")) multiplexer_5 (
    .in0(Entrada_A[27]), .in1(Entrada_A[28]), .out(\Saída_A [27]), .sel(in_2));
  Multiplexer #(.enable("false")) multiplexer_6 (
    .in0(Entrada_A[26]), .in1(Entrada_A[27]), .out(\Saída_A [26]), .sel(in_2));
  Multiplexer #(.enable("false")) multiplexer_7 (
    .in0(Entrada_A[25]), .in1(Entrada_A[26]), .out(\Saída_A [25]), .sel(in_2));
  Multiplexer #(.enable("false")) multiplexer_8 (
    .in0(Entrada_A[24]), .in1(Entrada_A[25]), .out(\Saída_A [24]), .sel(in_2));
  Multiplexer #(.enable("false")) multiplexer_9 (
    .in0(Entrada_A[23]), .in1(Entrada_A[24]), .out(\Saída_A [23]), .sel(in_2));
  Multiplexer #(.enable("false")) multiplexer_10 (
    .in0(Entrada_A[22]), .in1(Entrada_A[23]), .out(\Saída_A [22]), .sel(in_2));
  Multiplexer #(.enable("false")) multiplexer_11 (
    .in0(Entrada_A[21]), .in1(Entrada_A[22]), .out(\Saída_A [21]), .sel(in_2));
  Multiplexer #(.enable("false")) multiplexer_12 (
    .in0(Entrada_A[20]), .in1(Entrada_A[21]), .out(\Saída_A [20]), .sel(in_2));
  Multiplexer #(.enable("false")) multiplexer_13 (
    .in0(Entrada_A[19]), .in1(Entrada_A[20]), .out(\Saída_A [19]), .sel(in_2));
  Multiplexer #(.enable("false")) multiplexer_14 (
    .in0(Entrada_A[18]), .in1(Entrada_A[19]), .out(\Saída_A [18]), .sel(in_2));
  Multiplexer #(.enable("false")) multiplexer_15 (
    .in0(Entrada_A[17]), .in1(Entrada_A[18]), .out(\Saída_A [17]), .sel(in_2));
  Multiplexer #(.enable("false")) multiplexer_16 (
    .in0(Entrada_A[16]), .in1(Entrada_A[17]), .out(\Saída_A [16]), .sel(in_2));
  Multiplexer #(.enable("false")) multiplexer_17 (
    .in0(Entrada_A[15]), .in1(Entrada_A[16]), .out(\Saída_A [15]), .sel(in_2));
  Multiplexer #(.enable("false")) multiplexer_18 (
    .in0(Entrada_A[14]), .in1(Entrada_A[15]), .out(\Saída_A [14]), .sel(in_2));
  Multiplexer #(.enable("false")) multiplexer_19 (
    .in0(Entrada_A[13]), .in1(Entrada_A[14]), .out(\Saída_A [13]), .sel(in_2));
  Multiplexer #(.enable("false")) multiplexer_20 (
    .in0(Entrada_A[12]), .in1(Entrada_A[13]), .out(\Saída_A [12]), .sel(in_2));
  Multiplexer #(.enable("false")) multiplexer_21 (
    .in0(Entrada_A[11]), .in1(Entrada_A[12]), .out(\Saída_A [11]), .sel(in_2));
  Multiplexer #(.enable("false")) multiplexer_22 (
    .in0(Entrada_A[10]), .in1(Entrada_A[11]), .out(\Saída_A [10]), .sel(in_2));
  Multiplexer #(.enable("false")) multiplexer_23 (
    .in0(Entrada_A[9]), .in1(Entrada_A[10]), .out(\Saída_A [9]), .sel(in_2));
  Multiplexer #(.enable("false")) multiplexer_24 (
    .in0(Entrada_A[8]), .in1(Entrada_A[9]), .out(\Saída_A [8]), .sel(in_2));
  Multiplexer #(.enable("false")) multiplexer_25 (
    .in0(Entrada_A[7]), .in1(Entrada_A[8]), .out(\Saída_A [7]), .sel(in_2));
  Multiplexer #(.enable("false")) multiplexer_26 (
    .in0(Entrada_A[6]), .in1(Entrada_A[7]), .out(\Saída_A [6]), .sel(in_2));
  Multiplexer #(.enable("false")) multiplexer_27 (
    .in0(Entrada_A[5]), .in1(Entrada_A[6]), .out(\Saída_A [5]), .sel(in_2));
  Multiplexer #(.enable("false")) multiplexer_28 (
    .in0(Entrada_A[4]), .in1(Entrada_A[5]), .out(\Saída_A [4]), .sel(in_2));
  Multiplexer #(.enable("false")) multiplexer_29 (
    .in0(Entrada_A[3]), .in1(Entrada_A[4]), .out(\Saída_A [3]), .sel(in_2));
  Multiplexer #(.enable("false")) multiplexer_30 (
    .in0(Entrada_A[2]), .in1(Entrada_A[3]), .out(\Saída_A [2]), .sel(in_2));
  Multiplexer #(.enable("false")) multiplexer_31 (
    .in0(Entrada_A[1]), .in1(Entrada_A[2]), .out(\Saída_A [1]), .sel(in_2));
  Multiplexer #(.enable("false")) multiplexer_32 (.in0(Entrada_A[0]), .in1(1'b0), .out(\Saída_A [0]), .sel(in_2));
endmodule
